# Fritzing sketch Christmas Tree (saved by Fritzing 0.9.2b)
breadboards: 1

parts:
  LED1 = smd LED [color="Yellow (574nm)" package="0805 [SMD]"]
  LED3 = smd LED [color="Green (560nm)" package="0805 [SMD]"]
  LED4 = smd LED [color="Red (635nm)" package="0805 [SMD]"]
  LED5 = smd LED [color="Red (660nm)" package="0805 [SMD]"]
  Part1 = Arduino Nano (Rev3.0)
  LED6 = smd LED [color="Yellow (574nm)" package="0805 [SMD]"]

nets:
  N1: LED1.cathode, LED3.cathode, LED4.cathode, LED5.cathode, Part1.GND, LED6.cathode
