# Fritzing sketch Christmas Tree (saved by Fritzing 0.9.3b)
breadboards: 1

parts:
  IC1 = MICROCONTROLLER [package=dil28-3-simon-kit]
  S1 = Pushbutton [package="[THT]"]
  XTAL1 = Crystal [frequency="16 Mhz" package=THT]
  C1 = Ceramic Capacitor [capacitance=100nF package="100 mil [THT, multilayer]"]
  C2 = Ceramic Capacitor [capacitance=100nF package="100 mil [THT, multilayer]"]
  R1 = Resistor [tolerance=±5% resistance=10k package=THT]
  R2 = Resistor [tolerance=±5% resistance=220 package=THT]
  LED1 = LED - 5mm [color="Green (570nm)" package="5 mm [THT]"]
  J1 = Screw terminal - 2 pins [package=THT]

nets:
  N1: IC1.PC6(_RESET), S1.Pin_1, S1.Pin_2, R1.Pin_1
  N2: IC1.VCC, R1.Pin_0, J1.pin1
  N3: IC1.GND, S1.Pin_3, S1.Pin_4, C1.0, C2.0, R2.Pin_1, J1.pin2
  N4: IC1.PB6(XTAL1_TOSC1), XTAL1.pin_0, C1.1
  N5: IC1.PB7(XTAL2_TOSC2), XTAL1.pin_1, C2.1
  N6: IC1.PB5(SCK), LED1.anode
  N7: R2.Pin_0, LED1.cathode
